// Logisim project JOBY 11.circ as structural Verilog: 1 circuit, main circuit main
module main (
  input  A1,
  input  B1,
  input  B0,
  input  in_4,
  input  in_5
);

  wire and_1_out, xnor_1_out, xnor_2_out;

  // XNOR_Gate xnor_1 has open pins: out=xnor_1_out
  // XNOR_Gate xnor_2 has open pins: out=xnor_2_out
  and and_1 (and_1_out, xnor_1_out, xnor_2_out);

  // Notes on the sheet:
  //   A0
endmodule
